# Fritzing sketch rp_project_circuit (saved by Fritzing 0.9.10b)
breadboards: 1

parts:
  DHT11_1 = DHT11 module
  LED1 = smd LED [color="Red (633nm)" package="0805 [SMD]"]
  R1 = Photocell (LDR) [package=THT]
  S1 = KY-026
  R3 = Resistor [tolerance=±5% power=0.25 resistance=220 package=THT]
  R4 = Resistor [tolerance=±5% power=0.25 resistance=220 package=THT]
  R5 = Resistor [tolerance=±5% power=0.25 resistance=220 package=THT]
  J1 = STM32 Nucleo boards

nets:
  VCC: DHT11_1.VCC, R1.pin_0, J1.5V
  GND: DHT11_1.GND, LED1.cathode, S1.pin2, R3.Pin_1, R5.Pin_1, J1.GND
  N1: DHT11_1.DATA, J1.A2
  N2: LED1.anode, R4.Pin_0
  N3: R1.pin_1, R5.Pin_0, J1.A4/SDA
  N4: S1.pin1, J1.A3
  N5: S1.pin3, R3.Pin_0
  N6: R4.Pin_1, J1.D7

custom parts:
  DHT11 module: DHT11 black pcb module
  KY-026: ky-026 flame sensor module
